# Fritzing sketch Montage PMF (saved by Fritzing 0.9.3b)
breadboards: 1

parts:
  Composant2 = Arduino Uno (Rev3)
  Q1 = Basic FET P-Channel [package="D2Pak [SMD]"]
  RHT5 = Humidity and Temperature Sensor RHT03
  VCC1 = Battery block 9V
  J2 = Peltier Element
  R2 = Resistor [tolerance=±5% resistance=10k package=THT]
  RHT6 = Humidity and Temperature Sensor RHT03
  R3 = Resistor [tolerance=±5% resistance=10k package=THT]

nets:
  N1: Composant2.A0, R3.Pin_1
  N2: Composant2.GND, RHT5.GND_2, VCC1.-, J2.pin2, RHT6.GND_2
  N3: Composant2.D2, R2.Pin_1
  N4: Composant2.D5_PWM, Q1.Gate
  VCC: Composant2.5V, Q1.source, RHT5.Vcc, VCC1.+, RHT6.Vcc
  N5: Q1.drain, J2.pin1
  N6: RHT5.Data-signal, R2.Pin_0
  N7: RHT6.Data-signal, R3.Pin_0

notes:
  Connexion usb pour le module peltier
  Module peltier pour refroidir la canette
  Capteur DHT22 pour mesurer la température interieure du frigo
  Capteur DHT22 pour mesurer la temperature extérieure
